# Fritzing sketch breadboard_setup (saved by Fritzing 0.9.3b)
breadboards: 1

parts:
  R1 = Rotary Potentiometer (Small) [maximum_resistance=100kΩ package=THT]
  LED1 = LED - 5mm [color="Red (633nm)" package="5 mm [THT]"]
  Part1 = Arduino Nano (Rev3.0)
  R2 = Resistor [tolerance=±5% resistance=220 package="2512 [SMD]"]

nets:
  N1: R1.leg1, Part1.5V
  N2: R1.wiper, Part1.A0
  N3: R1.leg2, LED1.cathode, Part1.GND
  N4: LED1.anode, R2.Pin_0
  N5: Part1.D6, R2.Pin_1
